// Logisim project Module13.circ as structural Verilog
module Lecture_C_m4_counter (
  output out_1,
  output out_2
);

  wire blackbox_1_q0new, blackbox_1_q1new, clock_1_out;

  Clock clock_1 (.out(clock_1_out));
  BlackBox blackbox_1 (.Q0(out_1), .Q1(out_2), .C(clock_1_out), .Q0new(blackbox_1_q0new), .Q1new(blackbox_1_q1new));
  D_Flip_Flop Q0 (.clk(clock_1_out), .D(blackbox_1_q0new), .Q(out_1));  // open: Qn, preset, en, reset
  D_Flip_Flop Q1 (.clk(clock_1_out), .D(blackbox_1_q1new), .Q(out_2));  // open: Qn, preset, en, reset
endmodule

module BlackBox (
  input  Q0,
  input  Q1,
  input  C,
  output Q0new,
  output Q1new
);

  wire and_1_out, and_2_out, and_3_out, and_4_out, and_5_out, not_1_out, not_2_out, not_3_out, not_4_out;

  not not_1 (not_1_out, Q0);
  not not_2 (not_2_out, C);
  not not_3 (not_3_out, Q1);
  not not_4 (not_4_out, not_2_out);
  and and_1 (and_1_out, Q0, not_4_out);
  and and_2 (and_2_out, not_1_out, not_2_out);
  and and_3 (and_3_out, Q0, not_3_out);
  and and_4 (and_4_out, Q0, not_4_out);
  and and_5 (and_5_out, not_1_out, Q1, not_2_out);
  or or_1 (Q0new, and_1_out, and_2_out);
  or or_2 (Q1new, and_3_out, and_4_out, and_5_out);
endmodule

module Lecture_D_8_Bit_Rom_Chip (
  input  Q0,
  input  Q1,
  input  C,
  output Q0new,
  output Q1new
);

  wire [2:2] not_1_out;

  not not_1 (not_1_out[2], C);
  ROM #(.addrWidth(3), .dataWidth(2)) rom_1 (.addr({not_1_out[2], Q1, Q0}), .data({Q1new, Q0new}));  // open: sel

  // Notes on the sheet:
  //   contents of rom_1 (hex, n*v repeats v):
  //   0 1 1 2 2 3 3
endmodule

module LD_simplified_BBR (
  input  Q0,
  input  Q1,
  output Q0new,
  output Q1new
);

  ROM #(.addrWidth(2), .dataWidth(2)) rom_1 (.addr({Q1, Q0}), .data({Q1new, Q0new}));  // open: sel

  // Notes on the sheet:
  //   contents of rom_1 (hex, n*v repeats v):
  //   1 2 3
endmodule

module Lecture_D_4_bit_mod_16_counter (
  output [3:0] out_1
);

  wire clock_1_out, d_ff_1_qn, d_ff_2_qn, d_ff_3_qn, d_ff_4_qn;

  Clock clock_1 (.out(clock_1_out));
  D_Flip_Flop d_ff_1 (.clk(clock_1_out), .D(d_ff_1_qn), .Q(out_1[0]), .Qn(d_ff_1_qn));  // open: preset, en, reset
  D_Flip_Flop d_ff_2 (.clk(d_ff_1_qn), .D(d_ff_2_qn), .Q(out_1[1]), .Qn(d_ff_2_qn));  // open: preset, en, reset
  D_Flip_Flop d_ff_3 (.clk(d_ff_2_qn), .D(d_ff_3_qn), .Q(out_1[2]), .Qn(d_ff_3_qn));  // open: preset, en, reset
  D_Flip_Flop d_ff_4 (.clk(d_ff_3_qn), .D(d_ff_4_qn), .Q(out_1[3]), .Qn(d_ff_4_qn));  // open: preset, en, reset
endmodule

module Test_1 (
  output Q0new,
  output Q1new
);

  wire clock_1_out;
  wire [1:0] rom_1_data;

  ROM #(.addrWidth(2), .dataWidth(2)) rom_1 (.addr({Q1new, Q0new}), .data(rom_1_data));  // open: sel
  Clock clock_1 (.out(clock_1_out));
  D_Flip_Flop d_ff_1 (.clk(clock_1_out), .D(rom_1_data[0]), .Q(Q0new));  // open: Qn, preset, en, reset
  D_Flip_Flop d_ff_2 (.clk(clock_1_out), .D(rom_1_data[1]), .Q(Q1new));  // open: Qn, preset, en, reset

  // Notes on the sheet:
  //   contents of rom_1 (hex, n*v repeats v):
  //   1 2 3
endmodule
