// Logisim project Module12.circ as structural Verilog: 18 circuits, main circuit main
module main (
  input  in_1,
  input  in_2,
  output out_3,
  output out_4
);

  HalfAdder halfadder_1 (.Input_X(in_1), .Input_Y(in_2), .Sum(out_3), .Carry(out_4));

  // Notes on the sheet:
  //   Half Adder
endmodule

module HalfAdder (
  input  Input_X,
  input  Input_Y,
  output Sum,
  output Carry
);

  xor xor_1 (Sum, Input_X, Input_Y);
  and and_1 (Carry, Input_X, Input_Y);
endmodule

module FullAdder (
  input  Input_X,
  input  Input_Y,
  input  Cin,
  output Sum,
  output Cout
);

  wire halfadder_1_carry, halfadder_1_sum, halfadder_2_carry;

  HalfAdder halfadder_1 (.Input_X(Input_X), .Input_Y(Input_Y), .Sum(halfadder_1_sum), .Carry(halfadder_1_carry));
  HalfAdder halfadder_2 (.Input_X(halfadder_1_sum), .Input_Y(Cin), .Sum(Sum), .Carry(halfadder_2_carry));
  or or_1 (Cout, halfadder_2_carry, halfadder_1_carry);
endmodule

module RippleCarry_4_BitAdder (
  input  Cin,
  input  X0,
  input  Y0,
  input  X1,
  input  Y1,
  input  X2,
  input  Y2,
  input  X3,
  input  Y3,
  output S0,
  output S1,
  output S2,
  output S3,
  output Cout
);

  wire fulladder_1_cout, fulladder_2_cout, fulladder_3_cout;

  FullAdder fulladder_1 (.Input_X(Cin), .Input_Y(X0), .Cin(Y0), .Sum(S0), .Cout(fulladder_1_cout));
  FullAdder fulladder_2 (.Input_X(fulladder_1_cout), .Input_Y(X1), .Cin(Y1), .Sum(S1), .Cout(fulladder_2_cout));
  FullAdder fulladder_3 (.Input_X(fulladder_2_cout), .Input_Y(X2), .Cin(Y2), .Sum(S2), .Cout(fulladder_3_cout));
  FullAdder fulladder_4 (.Input_X(fulladder_3_cout), .Input_Y(X3), .Cin(Y3), .Sum(S3), .Cout(Cout));

  // Notes on the sheet:
  //   Can do addition, and because we can do addition that means we can do multiplication and division
endmodule

module _1_s_Complement_of_Y (
  input  Flag,
  input  X0,
  input  Y0,
  input  X1,
  input  Y1,
  input  X2,
  input  Y2,
  input  X3,
  input  Y3,
  output S0,
  output S1,
  output S2,
  output S3
);

  wire fulladder_1_cout, fulladder_2_cout, fulladder_3_cout, xor_1_out, xor_2_out, xor_3_out, xor_4_out;

  xor xor_1 (xor_1_out, Flag, Y0);
  xor xor_2 (xor_2_out, Flag, Y1);
  xor xor_3 (xor_3_out, Flag, Y2);
  xor xor_4 (xor_4_out, Flag, Y3);
  FullAdder fulladder_1 (.Input_X(Flag), .Input_Y(X0), .Cin(xor_1_out), .Sum(S0), .Cout(fulladder_1_cout));
  FullAdder fulladder_2 (.Input_X(fulladder_1_cout), .Input_Y(X1), .Cin(xor_2_out), .Sum(S1), .Cout(fulladder_2_cout));
  FullAdder fulladder_3 (.Input_X(fulladder_2_cout), .Input_Y(X2), .Cin(xor_3_out), .Sum(S2), .Cout(fulladder_3_cout));
  FullAdder fulladder_4 (.Input_X(fulladder_3_cout), .Input_Y(X3), .Cin(xor_4_out), .Sum(S3));  // open: Cout

  // Notes on the sheet:
  //   Adding a 1's Complement of Y
  //   X + Y'
  //   If Flag is 0 it's an Adder if Flag is 0 it's a subtractor
endmodule

module Decoder (
  input  [1:0] in_1,
  output O0,
  output O1,
  output O2,
  output O3
);

  wire not_1_out, not_2_out;

  not not_1 (not_1_out, in_1[0]);
  not not_2 (not_2_out, in_1[1]);
  and u_O0 (O0, not_1_out, not_2_out);
  and u_O1 (O1, in_1[0], not_2_out);
  and u_O2 (O2, not_1_out, in_1[1]);
  and u_O3 (O3, in_1[0], in_1[1]);
endmodule

module mp_Lecture (
  input  [7:0] in_1,
  input  [7:0] in_2,
  input  [7:0] in_3,
  input  [7:0] in_4,
  input  [1:0] Select_Bits,
  output [7:0] out_6
);

  wire [7:0] multiplexer_1_out, multiplexer_2_out;

  Multiplexer #(.width(8)) multiplexer_1 (
    .in0(in_1), .in1(in_2), .out(multiplexer_1_out), .sel(Select_Bits[0]));  // open: en
  Multiplexer #(.width(8)) multiplexer_2 (
    .in0(in_3), .in1(in_4), .out(multiplexer_2_out), .sel(Select_Bits[0]));  // open: en
  Multiplexer #(.width(8)) multiplexer_3 (
    .in0(multiplexer_1_out), .in1(multiplexer_2_out), .out(out_6), .sel(Select_Bits[1]));  // open: en
endmodule

module HW_8_BitAdder (
  input  Cin,
  input  X0,
  input  Y0,
  input  X1,
  input  Y1,
  input  X2,
  input  Y2,
  input  X3,
  input  Y3,
  input  X4,
  input  Y4,
  input  X5,
  input  Y5,
  input  X6,
  input  Y6,
  input  X7,
  input  Y7,
  output S0,
  output S1,
  output S2,
  output S3,
  output S4,
  output S5,
  output S6,
  output S7,
  output Cout
);

  wire fulladder_1_cout, fulladder_2_cout, fulladder_3_cout, fulladder_4_cout, fulladder_5_cout,
       fulladder_6_cout, fulladder_7_cout;

  FullAdder fulladder_1 (.Input_X(Cin), .Input_Y(X0), .Cin(Y0), .Sum(S0), .Cout(fulladder_1_cout));
  FullAdder fulladder_2 (.Input_X(fulladder_1_cout), .Input_Y(X1), .Cin(Y1), .Sum(S1), .Cout(fulladder_2_cout));
  FullAdder fulladder_3 (.Input_X(fulladder_2_cout), .Input_Y(X2), .Cin(Y2), .Sum(S2), .Cout(fulladder_3_cout));
  FullAdder fulladder_4 (.Input_X(fulladder_3_cout), .Input_Y(X3), .Cin(Y3), .Sum(S3), .Cout(fulladder_4_cout));
  FullAdder fulladder_5 (.Input_X(fulladder_4_cout), .Input_Y(X4), .Cin(Y4), .Sum(S4), .Cout(fulladder_5_cout));
  FullAdder fulladder_6 (.Input_X(fulladder_5_cout), .Input_Y(X5), .Cin(Y5), .Sum(S5), .Cout(fulladder_6_cout));
  FullAdder fulladder_7 (.Input_X(fulladder_6_cout), .Input_Y(X6), .Cin(Y6), .Sum(S6), .Cout(fulladder_7_cout));
  FullAdder fulladder_8 (.Input_X(fulladder_7_cout), .Input_Y(X7), .Cin(Y7), .Sum(S7), .Cout(Cout));

  // Notes on the sheet:
  //   8-BitAdder
endmodule

module full_adder_decoder (
  input  in_1,
  input  in_2,
  input  in_3,
  output out_4,
  output out_5,
  output out_6,
  output out_7,
  output out_8,
  output out_9,
  output out_10,
  output out_11
);

  wire not_1_out, not_2_out, not_3_out;

  not not_1 (not_1_out, in_1);
  not not_2 (not_2_out, in_2);
  not not_3 (not_3_out, in_3);
  and and_1 (out_4, not_1_out, not_2_out, not_3_out);
  and and_2 (out_5, not_1_out, not_2_out, in_3);
  and and_3 (out_6, not_1_out, in_2, not_3_out);
  and and_4 (out_7, not_1_out, in_2, in_3);
  and and_5 (out_8, in_1, not_2_out, not_3_out);
  and and_6 (out_9, in_1, not_2_out, in_3);
  and and_7 (out_10, in_1, in_2, not_3_out);
  and and_8 (out_11, in_1, in_2, in_3);
endmodule

module _1_bit_decoder (
  input  X,
  input  Y,
  input  Cin,
  output Sum,
  output Cout
);

  wire full_adder_decoder_1_out_5, full_adder_decoder_1_out_6, full_adder_decoder_1_out_7,
       full_adder_decoder_1_out_8, full_adder_decoder_1_out_9, full_adder_decoder_1_out_10,
       full_adder_decoder_1_out_11;

  full_adder_decoder full_adder_decoder_1 (
    .in_1(X), .in_2(Y), .in_3(Cin), .out_5(full_adder_decoder_1_out_5), .out_6(full_adder_decoder_1_out_6),
    .out_7(full_adder_decoder_1_out_7), .out_8(full_adder_decoder_1_out_8),
    .out_9(full_adder_decoder_1_out_9), .out_10(full_adder_decoder_1_out_10),
    .out_11(full_adder_decoder_1_out_11));  // open: out_4
  or or_1 (Sum, full_adder_decoder_1_out_5, full_adder_decoder_1_out_6, full_adder_decoder_1_out_8, full_adder_decoder_1_out_11);
  or or_2 (Cout, full_adder_decoder_1_out_7, full_adder_decoder_1_out_9, full_adder_decoder_1_out_10, full_adder_decoder_1_out_11);
endmodule

module HW_4_bit_decoder (
  input  Cin,
  input  X0,
  input  Y0,
  input  X1,
  input  Y1,
  input  X2,
  input  Y2,
  input  X3,
  input  Y3,
  output S0,
  output S1,
  output S2,
  output Cout
);

  wire n1_bit_decoder_1_cout, n1_bit_decoder_2_cout, n1_bit_decoder_3_cout;

  _1_bit_decoder u_1_bit_decoder_1 (.X(Y0), .Y(X0), .Cin(Cin), .Sum(S0), .Cout(n1_bit_decoder_1_cout));
  _1_bit_decoder u_1_bit_decoder_2 (
    .X(Y1), .Y(X1), .Cin(n1_bit_decoder_1_cout), .Sum(S1), .Cout(n1_bit_decoder_2_cout));
  _1_bit_decoder u_1_bit_decoder_3 (
    .X(Y2), .Y(X2), .Cin(n1_bit_decoder_2_cout), .Sum(S2), .Cout(n1_bit_decoder_3_cout));
  _1_bit_decoder u_1_bit_decoder_4 (.X(Y3), .Y(X3), .Cin(n1_bit_decoder_3_cout), .Sum(Cout));  // open: Cout
endmodule

module HW_Multiplexer_8_to_2 (
  input  [1:0] _0,
  input  [1:0] _1,
  input  [1:0] _2,
  input  [1:0] _3,
  input  [1:0] _4,
  input  [1:0] _5,
  input  [1:0] _6,
  input  [1:0] _7,
  input  [2:0] Select_Bits,
  output [1:0] out_10
);

  Multiplexer #(.select(3)) multiplexer_1 (
    .in0(_0[0]), .in1(_1[0]), .in2(_2[0]), .in3(_3[0]), .in4(_4[0]), .in5(_5[0]), .in6(_6[0]), .in7(_7[0]),
    .out(out_10[0]), .sel(Select_Bits));  // open: en
  Multiplexer #(.select(3)) multiplexer_2 (
    .in0(_7[1]), .in1(_6[1]), .in2(_5[1]), .in3(_4[1]), .in4(_3[1]), .in5(_2[1]), .in6(_1[1]), .in7(_0[1]),
    .out(out_10[1]), .sel(Select_Bits));  // open: en
endmodule

module mp_4_to_1 (
  input  _0,
  input  _1,
  input  _2,
  input  _3,
  input  [1:0] Select_Bits,
  output Y
);

  Multiplexer #(.select(2)) multiplexer_1 (
    .in0(_0), .in1(_1), .in2(_2), .in3(_3), .out(Y), .sel(Select_Bits));  // open: en
endmodule

module mp_4_to_2 (
  input  [1:0] in_1,
  input  [1:0] in_2,
  input  [1:0] in_3,
  input  [1:0] in_4,
  input  [1:0] in_5,
  output [1:0] out_6
);

  Multiplexer #(.select(2)) multiplexer_1 (
    .in0(in_1[0]), .in1(in_2[0]), .in2(in_3[0]), .in3(in_4[0]), .out(out_6[0]), .sel(in_5));  // open: en
  Multiplexer #(.select(2)) multiplexer_2 (
    .in0(in_1[1]), .in1(in_2[1]), .in2(in_3[1]), .in3(in_4[1]), .out(out_6[1]), .sel(in_5));  // open: en
endmodule

module mp_8_to_1 (
  input  _0,
  input  _1,
  input  _2,
  input  _3,
  input  _4,
  input  _5,
  input  _6,
  input  _7,
  input  [2:0] Select_Bits,
  output Y
);

  Multiplexer #(.select(3)) multiplexer_1 (
    .in0(_0), .in1(_1), .in2(_2), .in3(_3), .in4(_4), .in5(_5), .in6(_6), .in7(_7), .out(Y), .sel(Select_Bits));  // open: en
endmodule

module Practice_mp_16_to_1 (
  input  _0,
  input  _1,
  input  _2,
  input  _3,
  input  _4,
  input  _5,
  input  _6,
  input  _7,
  input  _8,
  input  _9,
  input  _10,
  input  _11,
  input  _12,
  input  _13,
  input  _14,
  input  _15,
  input  [3:0] Select_Bits,
  output Y
);

  Multiplexer #(.select(4)) multiplexer_1 (
    .in0(_0), .in1(_1), .in2(_2), .in3(_3), .in4(_4), .in5(_5), .in6(_6), .in7(_7), .in8(_8), .in9(_9),
    .in10(_10), .in11(_11), .in12(_12), .in13(_13), .in14(_14), .in15(_15), .out(Y), .sel(Select_Bits));  // open: en
endmodule

module mp_2_to_1 (
  input  _0,
  input  _1,
  input  Select_Bits,
  output Y
);

  Multiplexer multiplexer_1 (.in0(_0), .in1(_1), .out(Y), .sel(Select_Bits));  // open: en
endmodule

module HW_16_to_1_8_bit_mp (
  input  _0,
  input  _1,
  input  _2,
  input  _3,
  input  in_5,
  input  in_6,
  input  [1:0] Select_Bits,
  input  in_8,
  input  _0_2,
  input  _1_2,
  input  _2_2,
  input  _3_2,
  input  [1:0] Select_Bits_2,
  input  _0_3,
  input  _1_3,
  input  _2_3,
  input  _3_3,
  input  in_18,
  input  in_19,
  input  in_20,
  input  [1:0] Select_Bits_3,
  input  in_22,
  input  in_23,
  input  in_24,
  input  _0_4,
  input  _1_4,
  input  _2_4,
  input  _3_4,
  input  in_29,
  input  [1:0] Select_Bits_4,
  output out_31
);

  wire and_1_out, and_2_out, and_3_out, and_4_out, and_5_out, and_6_out, multiplexer_1_out,
       multiplexer_2_out, multiplexer_3_out, multiplexer_4_out, not_1_out, not_2_out, not_3_out, or_1_out,
       or_2_out;

  Multiplexer #(.select(2)) multiplexer_1 (
    .in0(_0), .in1(_1), .in2(_2), .in3(_3), .out(multiplexer_1_out), .sel({in_6, in_5}));  // open: en
  Multiplexer #(.select(2)) multiplexer_2 (
    .in0(_0_2), .in1(_1_2), .in2(_2_2), .in3(_3_2), .out(multiplexer_2_out), .sel({in_6, in_5}));  // open: en
  Multiplexer #(.select(2)) multiplexer_3 (
    .in0(_0_3), .in1(_1_3), .in2(_2_3), .in3(_3_3), .out(multiplexer_3_out), .sel({in_20, in_18}));  // open: en
  not not_1 (not_1_out, in_8);
  not not_2 (not_2_out, in_23);
  Multiplexer #(.select(2)) multiplexer_4 (
    .in0(_0_4), .in1(_1_4), .in2(_2_4), .in3(_3_4), .out(multiplexer_4_out), .sel({in_20, in_18}));  // open: en
  and and_1 (and_1_out, multiplexer_1_out, not_1_out);
  and and_2 (and_2_out, in_8, multiplexer_2_out);
  and and_3 (and_3_out, multiplexer_3_out, not_2_out);
  and and_4 (and_4_out, in_23, multiplexer_4_out);
  or or_1 (or_1_out, and_1_out, and_2_out);
  not not_3 (not_3_out, in_29);
  or or_2 (or_2_out, and_3_out, and_4_out);
  and and_5 (and_5_out, or_1_out, not_3_out);
  and and_6 (and_6_out, in_29, or_2_out);
  or or_3 (out_31, and_5_out, and_6_out);

  assign Select_Bits = {in_6, in_5};
  assign Select_Bits_2 = {in_6, in_5};
  assign Select_Bits_3 = {in_20, in_18};
  assign Select_Bits_4 = {in_20, in_18};
endmodule
